# Fritzing sketch Wire_APDS (saved by Fritzing 1.0.8)
breadboards: 1

parts:
  Mod1 = Raspberry Pi Pico W
  R1 = Resistor [tolerance=±1% power=0.25W resistance=50 package=THT]
  R2 = Resistor [tolerance=±1% power=0.25W resistance=50 package=THT]
  R3 = Resistor [tolerance=±1% power=0.25W resistance=50 package=THT]
  LED1 = RGB LED (com. cathode, rgb) [color="Red (633nm)" current=0.030A package="5 mm [THT]"]
  PART1 = APDS-9960 RGB and Gesture Sensor [part_number=SEN-12787]

nets:
  N1: Mod1.pin_3, Mod1.pin_8, Mod1.pin_13, Mod1.pin_18, Mod1.pin_23, Mod1.pin_28, Mod1.pin_33, Mod1.pin_38, LED1.common_cathode, PART1.GND
  N2: Mod1.pin_19, PART1.SDA
  N3: Mod1.pin_20, PART1.SCL
  N4: Mod1.pin_24, R2.Pin_1
  N5: Mod1.pin_25, R3.Pin_1
  N6: Mod1.pin_26, R1.Pin_1
  N7: Mod1.pin_36, PART1.VCC
  N8: R1.Pin_0, LED1.blue_anode
  N9: R2.Pin_0, LED1.red_anode
  N10: R3.Pin_0, LED1.green_anode

notes:
  Note: The actual board may look
  slightly different, but has the same pins

custom parts:
  Raspberry Pi Pico W: Raspberry Pi Pico W. Based around the RP2040 microcontroller the Pico W is a low cost microcontroller device bringing Raspberry Pi quality, cost, and easy of use to the microcontroller space. The areas marked KEEPOUT in pcb silkscreen should not have traces running through them to avoid shorts on a soldered in module!
  APDS-9960 RGB and Gesture Sensor: Breakout board for the Avago APDS-9960 proximity, light, RGB, and gesture sensors. Please visit www.sparkfun.com to learn more.
